# Fritzing sketch UbarCDC (saved by Fritzing 0.8.3b)
circuit board: 17.0394cm x 6.72509cm
breadboards: 1

parts:
  D24V3F3 = female pin header, 4 pins [form="♀ (female)"]
  BT-Mod = RN-52 BoB [form="♀ (female)" package=THT]
  BT_Conf = female pin header, 3 pins [form="♀ (female)"]
  RN-52 = female pin header, 1 pin [form="♀ (female)"]
  L9637D1 = L9637D BoB [chip_label=IC package="DIP (Dual Inline) [THT]"]
  R2 = Resistor [tolerance=±5% resistance=220 package=THT]
  R3 = Resistor [tolerance=±5% resistance=220 package=THT]
  R4 = Resistor [tolerance=±5% resistance=220 package=THT]
  Car = male pin header, 4 pins [form="♂ (male)"]
  R1 = Resistor [tolerance=±5% resistance=220 package=THT]
  Q1 = NPN-Transistor [package="TO92 [THT]"]
  Teensy_0-12 = male pin header, 14 pins [form="♂ (male)"]
  Teensy_13-23 = male pin header, 14 pins [form="♂ (male)"]
  Teensy_Side = male pin header, 5 pins [form="♂ (male)"]

nets:
  N1: D24V3F3.pin2, L9637D1.VS(13), R4.Pin_1, Car.pin3
  N2: D24V3F3.pin3, BT-Mod.GND(4), L9637D1.GND(9), Car.pin2, Teensy_0-12.pin1, Teensy_Side.pin3
  N3: D24V3F3.pin4, L9637D1.VCC(5), Q1.C, Teensy_Side.pin4
  N4: BT-Mod.TXD(1), Teensy_0-12.pin9
  N5: BT-Mod.RXD(2), Teensy_0-12.pin10
  N6: BT-Mod.VIN(3), Q1.E
  N7: BT-Mod.N/C#4, BT_Conf.pin1
  N8: BT-Mod.GPIO9, BT_Conf.pin2
  N9: BT-Mod.N/C#6, BT_Conf.pin3
  N10: BT-Mod.GPIO2, Teensy_0-12.pin8
  N11: RN-52.pin1, Teensy_0-12.pin7
  N12: L9637D1.TX(8), Teensy_0-12.pin11
  N13: L9637D1.RX(1), Teensy_0-12.pin12
  N14: L9637D1.K(11), Car.pin4
  N15: R2.Pin_0, R3.Pin_0, Teensy_13-23.pin2
  N16: R2.Pin_1, R3.Pin_1, R4.Pin_0, Teensy_13-23.pin6
  N17: R1.Pin_0, Q1.B
  N18: R1.Pin_1, Teensy_0-12.pin6

custom parts:
  RN-52 BoB: RN-52 Breakout board
  L9637D BoB: L9637D on a breakout board that is too large
